// Digital circuit 2's_Complement_Adder.dig as structural Verilog
module _2_s_Complement_Adder (
  input  inA_0,
  input  inA_1,
  input  inA_2,
  input  inA_3,
  input  inB_0,
  input  inB_1,
  input  inB_2,
  input  inB_3,
  input  op,
  output out0,
  output out1,
  output out2,
  output out3,
  output overflow
);

  wire FA0_c_o, FA1_c_o, FA2_c_o, FA3_c_o, xor_1_out, xor_3_out, xor_4_out, xor_5_out;

  xor xor_1 (xor_1_out, op, inB_3);
  Add FA3 (.a(inA_3), .b(xor_1_out), .c_i(FA2_c_o), .s(out3), .c_o(FA3_c_o));
  xor xor_2 (overflow, FA2_c_o, FA3_c_o);
  xor xor_3 (xor_3_out, op, inB_2);
  Add FA2 (.a(inA_2), .b(xor_3_out), .c_i(FA1_c_o), .s(out2), .c_o(FA2_c_o));
  xor xor_4 (xor_4_out, op, inB_1);
  Add FA1 (.a(inA_1), .b(xor_4_out), .c_i(FA0_c_o), .s(out1), .c_o(FA1_c_o));
  xor xor_5 (xor_5_out, op, inB_0);
  Add FA0 (.a(inA_0), .b(xor_5_out), .c_i(op), .s(out0), .c_o(FA0_c_o));

  // Notes on the sheet:
  //   Interface (do not edit the content inside this box)
  //   Inputs
  //   Result of doing the addition (op=0) / subtraction (op=1) and overflow bit:
  //   Output number (in 2's complement)
  //   First Number (in 2's complement)
  //   Second number (in 2's complement)
endmodule

/* Test case grading:
inA_0 inA_1 inA_2 inA_3 inB_0 inB_1 inB_2 inB_3 op out0 out1 out2 out3 overflow 

 0 0 0 0 0 0 0 0 0 0 0 0 0 0
 0 0 0 0 0 0 0 0 1 0 0 0 0 0
 0 0 0 0 0 0 0 1 0 0 0 0 1 0
 0 0 0 0 0 0 0 1 1 0 0 0 1 1
 0 0 0 0 0 0 1 0 0 0 0 1 0 0
 0 0 0 0 0 0 1 0 1 0 0 1 1 0
 0 0 0 0 0 0 1 1 0 0 0 1 1 0
 0 0 0 0 0 0 1 1 1 0 0 1 0 0
 0 0 0 0 0 1 0 0 0 0 1 0 0 0
 0 0 0 0 0 1 0 0 1 0 1 1 1 0
 0 0 0 0 0 1 0 1 0 0 1 0 1 0
 0 0 0 0 0 1 0 1 1 0 1 1 0 0
 0 0 0 0 0 1 1 0 0 0 1 1 0 0
 0 0 0 0 0 1 1 0 1 0 1 0 1 0
 0 0 0 0 0 1 1 1 0 0 1 1 1 0
 0 0 0 0 0 1 1 1 1 0 1 0 0 0
 0 0 0 0 1 0 0 0 0 1 0 0 0 0
 0 0 0 0 1 0 0 0 1 1 1 1 1 0
 0 0 0 0 1 0 0 1 0 1 0 0 1 0
 0 0 0 0 1 0 0 1 1 1 1 1 0 0
 0 0 0 0 1 0 1 0 0 1 0 1 0 0
 0 0 0 0 1 0 1 0 1 1 1 0 1 0
 0 0 0 0 1 0 1 1 0 1 0 1 1 0
 0 0 0 0 1 0 1 1 1 1 1 0 0 0
 0 0 0 0 1 1 0 0 0 1 1 0 0 0
 0 0 0 0 1 1 0 0 1 1 0 1 1 0
 0 0 0 0 1 1 0 1 0 1 1 0 1 0
 0 0 0 0 1 1 0 1 1 1 0 1 0 0
 0 0 0 0 1 1 1 0 0 1 1 1 0 0
 0 0 0 0 1 1 1 0 1 1 0 0 1 0
 0 0 0 0 1 1 1 1 0 1 1 1 1 0
 0 0 0 0 1 1 1 1 1 1 0 0 0 0
 0 0 0 1 0 0 0 0 0 0 0 0 1 0
 0 0 0 1 0 0 0 0 1 0 0 0 1 0
 0 0 0 1 0 0 0 1 0 0 0 0 0 1
 0 0 0 1 0 0 0 1 1 0 0 0 0 0
 0 0 0 1 0 0 1 0 0 0 0 1 1 0
 0 0 0 1 0 0 1 0 1 0 0 1 0 1
 0 0 0 1 0 0 1 1 0 0 0 1 0 1
 0 0 0 1 0 0 1 1 1 0 0 1 1 0
 0 0 0 1 0 1 0 0 0 0 1 0 1 0
 0 0 0 1 0 1 0 0 1 0 1 1 0 1
 0 0 0 1 0 1 0 1 0 0 1 0 0 1
 0 0 0 1 0 1 0 1 1 0 1 1 1 0
 0 0 0 1 0 1 1 0 0 0 1 1 1 0
 0 0 0 1 0 1 1 0 1 0 1 0 0 1
 0 0 0 1 0 1 1 1 0 0 1 1 0 1
 0 0 0 1 0 1 1 1 1 0 1 0 1 0
 0 0 0 1 1 0 0 0 0 1 0 0 1 0
 0 0 0 1 1 0 0 0 1 1 1 1 0 1
 0 0 0 1 1 0 0 1 0 1 0 0 0 1
 0 0 0 1 1 0 0 1 1 1 1 1 1 0
 0 0 0 1 1 0 1 0 0 1 0 1 1 0
 0 0 0 1 1 0 1 0 1 1 1 0 0 1
 0 0 0 1 1 0 1 1 0 1 0 1 0 1
 0 0 0 1 1 0 1 1 1 1 1 0 1 0
 0 0 0 1 1 1 0 0 0 1 1 0 1 0
 0 0 0 1 1 1 0 0 1 1 0 1 0 1
 0 0 0 1 1 1 0 1 0 1 1 0 0 1
 0 0 0 1 1 1 0 1 1 1 0 1 1 0
 0 0 0 1 1 1 1 0 0 1 1 1 1 0
 0 0 0 1 1 1 1 0 1 1 0 0 0 1
 0 0 0 1 1 1 1 1 0 1 1 1 0 1
 0 0 0 1 1 1 1 1 1 1 0 0 1 0
 0 0 1 0 0 0 0 0 0 0 0 1 0 0
 0 0 1 0 0 0 0 0 1 0 0 1 0 0
 0 0 1 0 0 0 0 1 0 0 0 1 1 0
 0 0 1 0 0 0 0 1 1 0 0 1 1 1
 0 0 1 0 0 0 1 0 0 0 0 0 1 1
 0 0 1 0 0 0 1 0 1 0 0 0 0 0
 0 0 1 0 0 0 1 1 0 0 0 0 0 0
 0 0 1 0 0 0 1 1 1 0 0 0 1 1
 0 0 1 0 0 1 0 0 0 0 1 1 0 0
 0 0 1 0 0 1 0 0 1 0 1 0 0 0
 0 0 1 0 0 1 0 1 0 0 1 1 1 0
 0 0 1 0 0 1 0 1 1 0 1 0 1 1
 0 0 1 0 0 1 1 0 0 0 1 0 1 1
 0 0 1 0 0 1 1 0 1 0 1 1 1 0
 0 0 1 0 0 1 1 1 0 0 1 0 0 0
 0 0 1 0 0 1 1 1 1 0 1 1 0 0
 0 0 1 0 1 0 0 0 0 1 0 1 0 0
 0 0 1 0 1 0 0 0 1 1 1 0 0 0
 0 0 1 0 1 0 0 1 0 1 0 1 1 0
 0 0 1 0 1 0 0 1 1 1 1 0 1 1
 0 0 1 0 1 0 1 0 0 1 0 0 1 1
 0 0 1 0 1 0 1 0 1 1 1 1 1 0
 0 0 1 0 1 0 1 1 0 1 0 0 0 0
 0 0 1 0 1 0 1 1 1 1 1 1 0 0
 0 0 1 0 1 1 0 0 0 1 1 1 0 0
 0 0 1 0 1 1 0 0 1 1 0 0 0 0
 0 0 1 0 1 1 0 1 0 1 1 1 1 0
 0 0 1 0 1 1 0 1 1 1 0 0 1 1
 0 0 1 0 1 1 1 0 0 1 1 0 1 1
 0 0 1 0 1 1 1 0 1 1 0 1 1 0
 0 0 1 0 1 1 1 1 0 1 1 0 0 0
 0 0 1 0 1 1 1 1 1 1 0 1 0 0
 0 0 1 1 0 0 0 0 0 0 0 1 1 0
 0 0 1 1 0 0 0 0 1 0 0 1 1 0
 0 0 1 1 0 0 0 1 0 0 0 1 0 1
 0 0 1 1 0 0 0 1 1 0 0 1 0 0
 0 0 1 1 0 0 1 0 0 0 0 0 0 0
 0 0 1 1 0 0 1 0 1 0 0 0 1 0
 0 0 1 1 0 0 1 1 0 0 0 0 1 0
 0 0 1 1 0 0 1 1 1 0 0 0 0 0
 0 0 1 1 0 1 0 0 0 0 1 1 1 0
 0 0 1 1 0 1 0 0 1 0 1 0 1 0
 0 0 1 1 0 1 0 1 0 0 1 1 0 1
 0 0 1 1 0 1 0 1 1 0 1 0 0 0
 0 0 1 1 0 1 1 0 0 0 1 0 0 0
 0 0 1 1 0 1 1 0 1 0 1 1 0 1
 0 0 1 1 0 1 1 1 0 0 1 0 1 0
 0 0 1 1 0 1 1 1 1 0 1 1 1 0
 0 0 1 1 1 0 0 0 0 1 0 1 1 0
 0 0 1 1 1 0 0 0 1 1 1 0 1 0
 0 0 1 1 1 0 0 1 0 1 0 1 0 1
 0 0 1 1 1 0 0 1 1 1 1 0 0 0
 0 0 1 1 1 0 1 0 0 1 0 0 0 0
 0 0 1 1 1 0 1 0 1 1 1 1 0 1
 0 0 1 1 1 0 1 1 0 1 0 0 1 0
 0 0 1 1 1 0 1 1 1 1 1 1 1 0
 0 0 1 1 1 1 0 0 0 1 1 1 1 0
 0 0 1 1 1 1 0 0 1 1 0 0 1 0
 0 0 1 1 1 1 0 1 0 1 1 1 0 1
 0 0 1 1 1 1 0 1 1 1 0 0 0 0
 0 0 1 1 1 1 1 0 0 1 1 0 0 0
 0 0 1 1 1 1 1 0 1 1 0 1 0 1
 0 0 1 1 1 1 1 1 0 1 1 0 1 0
 0 0 1 1 1 1 1 1 1 1 0 1 1 0
 0 1 0 0 0 0 0 0 0 0 1 0 0 0
 0 1 0 0 0 0 0 0 1 0 1 0 0 0
 0 1 0 0 0 0 0 1 0 0 1 0 1 0
 0 1 0 0 0 0 0 1 1 0 1 0 1 1
 0 1 0 0 0 0 1 0 0 0 1 1 0 0
 0 1 0 0 0 0 1 0 1 0 1 1 1 0
 0 1 0 0 0 0 1 1 0 0 1 1 1 0
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*/
